# Fritzing sketch Sensebender_Nrf95w (saved by Fritzing 0.9.3b)
circuit board: 3.38239cm x 2.17313cm
breadboards: 1

parts:
  RFM95W = RFM9xW
  Ant = SMA Antenna Connector [package=sma-edge]
  SB = double row female pin header, 8 pins [form="♀ (female)"]

nets:
  GND: RFM95W.GND, Ant.GND, SB.pin1
  N1: RFM95W.MISO, SB.pin4
  N2: RFM95W.MOSI, SB.pin6
  N3: RFM95W.SCK, SB.pin3
  N4: RFM95W.NSS, SB.pin7
  N5: RFM95W.ANT, Ant.SIGNAL
  N6: RFM95W.VCC, SB.pin8
  N7: RFM95W.DIO0, SB.pin5
  N8: RFM95W.DIO1, SB.pin2

custom parts:
  RFM9xW: RFM9xW Module connector
